# Fritzing sketch Tool_I2CScanner_Teil_2 (saved by Fritzing 0.9.3b)
breadboards: 1

parts:
  Bauteil2 = Arduino Nano (Rev3.0)
  0_91_Inch_I2C_OLED_Display1 = 0.91 Inch I2C OLED Display
  IC2 = 24LC256 [package=THT]
  R3 = Resistor [tolerance=±5% resistance=10k package="2010 [SMD]"]
  U1 = POT [package=pot_mammoth]
  R5 = Resistor [tolerance=±5% resistance=4.7k package=THT]
  S3 = Pushbutton [package="[SMD]"]
  R6 = Resistor [tolerance=±5% resistance=4.7k package=THT]

nets:
  GND: Bauteil2.GND, 0_91_Inch_I2C_OLED_Display1.GND, R3.Pin_0, U1.S, U1.E, S3.Pin_3, S3.Pin_4
  N1: Bauteil2.D2, S3.Pin_1, S3.Pin_2
  N2: Bauteil2.D4, IC2.SCL_-_I2C_Clock, R5.Pin_0
  N3: Bauteil2.D5, IC2.SDA_-_I2C_Data, R6.Pin_0
  N4: Bauteil2.D6, R5.Pin_1
  N5: Bauteil2.D7, R6.Pin_1
  5V: Bauteil2.5V, 0_91_Inch_I2C_OLED_Display1.VCC, IC2.+V
  N6: Bauteil2.A5, 0_91_Inch_I2C_OLED_Display1.SCK
  N7: Bauteil2.A4, 0_91_Inch_I2C_OLED_Display1.SDA
  N8: Bauteil2.A0, U1.A
  N9: IC2.A0, IC2.A1, IC2.A2, IC2.0V
  N10: IC2.WP_-_Write_Protect, R3.Pin_1

custom parts:
  0.91 Inch I2C OLED Display: Strong contrast by the use of the innovative OLED technology in the wide 0.91 inch Display! Due to the high resolution of 128x32 pixels the Display offers plenty of space to Display items! Easy connection of the display with Arduino, Raspberry Pi, and co. by I2C interface only four Pins! Thanks To The Standard Controller (SSD 1306) already libraries for Arduino, Raspberry Pi, and co. exist,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
