# Fritzing sketch Tool_I2CScanner_Teil_3 (saved by Fritzing 0.9.3b)
breadboards: 1

parts:
  Bauteil2 = Arduino Nano (Rev3.0)
  0_91_Inch_I2C_OLED_Display1 = 0.91 Inch I2C OLED Display
  R5 = Resistor [tolerance=±5% resistance=4.7k package=THT]
  S3 = Pushbutton [package="[SMD]"]
  R6 = Resistor [tolerance=±5% resistance=4.7k package=THT]
  S4 = Pushbutton [package="[SMD]"]
  S5 = Pushbutton [package="[SMD]"]
  R7 = Resistor [tolerance=±5% resistance=100 package=THT]
  R8 = Resistor [tolerance=±5% resistance=100 package=THT]
  D1 = Zener Diode [part_number=1N4732A breakdown_voltage=5.1V package="300 mil [THT]"]
  D2 = Zener Diode [part_number=1N4732A breakdown_voltage=5.1V package="300 mil [THT]"]
  J4 = BANANA_CONN [package=banana_conn]
  J5 = BANANA_CONN [package=banana_conn]
  J6 = BANANA_CONN [package=banana_conn]
  J7 = BANANA_CONN [package=banana_conn]

nets:
  GND: Bauteil2.GND, 0_91_Inch_I2C_OLED_Display1.GND, S3.Pin_3, S3.Pin_4, S4.Pin_3, S4.Pin_4, S5.Pin_3, S5.Pin_4, D1.anode, D2.anode, J6.1
  N1: Bauteil2.D2, S3.Pin_1, S3.Pin_2
  N2: Bauteil2.D4, R5.Pin_0, R8.Pin_1
  N3: Bauteil2.D5, R6.Pin_0, R7.Pin_1
  N4: Bauteil2.D6, R5.Pin_1
  N5: Bauteil2.D7, R6.Pin_1
  N6: Bauteil2.D8, S5.Pin_1, S5.Pin_2
  N7: Bauteil2.D9, S4.Pin_1, S4.Pin_2
  5V: Bauteil2.5V, 0_91_Inch_I2C_OLED_Display1.VCC, J7.1
  N8: Bauteil2.A5, 0_91_Inch_I2C_OLED_Display1.SCK
  N9: Bauteil2.A4, 0_91_Inch_I2C_OLED_Display1.SDA
  N10: Bauteil2.A1, R8.Pin_0, D1.cathode, J4.1
  N11: Bauteil2.A0, R7.Pin_0, D2.cathode, J5.1

custom parts:
  0.91 Inch I2C OLED Display: Strong contrast by the use of the innovative OLED technology in the wide 0.91 inch Display! Due to the high resolution of 128x32 pixels the Display offers plenty of space to Display items! Easy connection of the display with Arduino, Raspberry Pi, and co. by I2C interface only four Pins! Thanks To The Standard Controller (SSD 1306) already libraries for Arduino, Raspberry Pi, and co. exist,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
